# Fritzing sketch LedandSwitch (saved by Fritzing 0.9.1b)
breadboards: 1

parts:
  LED3 = LED - 5mm [color="Red (633nm)" package="5 mm [THT]"]
  R1 = Resistor [tolerance=±5% resistance=1k package=THT]
  Part2 = Particle Argon [part_number="Adafruit #3405"]
  S1 = Momentary Switch [package=ksa_sealed_tac_switch]
  R2 = Rotary Potentiometer (Small) [maximum_resistance=100kΩ package=THT]

nets:
  N1: LED3.cathode, R1.Pin_1
  N2: LED3.anode, Part2.SCL
  N3: R1.Pin_0, Part2.GND, S1.4, R2.leg1
  N4: Part2.SCK, R2.wiper
  N5: Part2.3V3, R2.leg2
  N6: Part2.IO14_A6, S1.2

custom parts:
  Particle Argon: Build on the Featherwing by Adafruit
