# Fritzing sketch LedSwitchPot (saved by Fritzing 0.9.1b)
breadboards: 1

parts:
  LED1 = LED - 5mm [color="Red (633nm)" package="5 mm [THT]"]
  R1 = Resistor [tolerance=±5% resistance=1k package=THT]
  Part1 = Photon
  S1 = Pushbutton [package="[THT]"]
  R2 = Rotary Potentiometer (Small) [maximum_resistance=10kΩ package=THT]

nets:
  N1: LED1.cathode, Part1.GND, S1.Pin_3, S1.Pin_4, R2.leg1
  N2: LED1.anode, R1.Pin_0
  N3: R1.Pin_1, Part1.D3
  N4: Part1.A0, R2.wiper
  N5: Part1.D4, S1.Pin_1, S1.Pin_2
  N6: Part1.3V3, R2.leg2
