# Fritzing sketch AmbientOrbCircuit (saved by Fritzing 0.9.1b)
breadboards: 1

parts:
  LED3 = LED - 5mm [color="Red (633nm)" package="5 mm [THT]"]
  R1 = Resistor [tolerance=±5% resistance=1k package=THT]
  Part2 = Particle Argon [part_number="Adafruit #3405"]
  S1 = Momentary Switch [package=ksa_sealed_tac_switch]
  R2 = Rotary Potentiometer (Small) [maximum_resistance=100kΩ package=THT]
  Part3 = Adafruit Breadboard-Friendly NeoPixel [part_number="Adafruit #1312"]

nets:
  N1: LED3.cathode, R1.Pin_1
  N2: LED3.anode, Part2.SCL
  GND: R1.Pin_0, Part2.GND, S1.4, R2.leg1, Part3.GND
  N3: Part2.SCK, R2.wiper
  3V3: Part2.3V3, R2.leg2, Part3.VDD
  N4: Part2.IO27_A10, Part3.IN
  N5: Part2.IO14_A6, S1.2

custom parts:
  Particle Argon: Build on the Featherwing by Adafruit
  Adafruit Breadboard-Friendly NeoPixel: This is the easiest way possible to add small, bright RGB pixels to your project. We took the same technology from our Flora NeoPixels and made them breadboard friendly, with two rows of 3 x 0.1" spaced header on each side for easy soldering, chaining and breadboarding. These ultra-bright LEDs have a constant-current driver cooked right into the LED package! The pixels are chainable - so you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
